# Fritzing sketch tmp36 (saved by Fritzing 0.9.0b)
breadboards: 1

parts:
  Part1 = Arduino Nano (Rev3.0)
  U1 = TMP36 [package=to-92-kit]

nets:
  GND: Part1.GND, U1.GND
  5V: Part1.5V, U1.VCC
  N1: Part1.A3, U1.VOUT
  N2: Part1.AREF, Part1.3V3
